# Fritzing sketch Кран-штабелер (saved by Fritzing 0.9.3b)

parts:
  Power_plug1 = Power plug
  A1 = Wemos S2 Mini [part_number="WeMos D1 Mini Lite"]
  Yumo-enc1 = YumoE6B2
  L298N1 = L298N DC motor driver
  M1 = DC Motor
  Yumo-enc2 = YumoE6B2
  M2 = DC Motor
  Yumo-enc3 = YumoE6B2
  M3 = DC Motor
  M4 = DC Motor
  L298N2 = L298N DC motor driver
  Power_plug2 = Power plug
  S1 = Limit Switch [package="Breakout Board"]
  S2 = Limit Switch [package="Breakout Board"]
  S3 = Limit Switch [package="Breakout Board"]
  S4 = Limit Switch [package="Breakout Board"]
  S5 = Limit Switch [package="Breakout Board"]
  Часть1 = Analog Digital MUX Breakout

nets:
  VCC: Power_plug1.VCC, A1.Pin_17, Yumo-enc1.V, L298N1.5V, Yumo-enc2.V, Yumo-enc3.V, L298N2.5V, S1.V, Часть1.VCC
  GND: Power_plug1.GND, A1.Pin_18, Yumo-enc1.GND, L298N1.GND, Yumo-enc2.GND, Yumo-enc3.GND, L298N2.GND, Power_plug2.GND, S1.G, Часть1.GND
  N1: A1.Pin_9, Часть1.SIG
  N2: A1.Pin_10, Часть1.S3
  N3: A1.Pin_11, Часть1.S2
  N4: A1.Pin_12, Часть1.S1
  N5: A1.Pin_13, Часть1.S0
  N6: A1.Pin_14, Часть1.EN
  N7: A1.Pin_19, L298N2.IN3
  N8: A1.Pin_20, L298N2.ENB
  N9: A1.Pin_21, L298N2.IN1
  N10: A1.Pin_22, L298N1.IN3
  N11: A1.Pin_23, L298N1.ENB
  N12: A1.Pin_24, L298N1.IN1
  N13: A1.Pin_27, L298N2.IN4
  N14: A1.Pin_28, L298N2.IN2
  N15: A1.Pin_29, L298N2.ENA
  N16: A1.Pin_30, L298N1.IN4
  N17: A1.Pin_31, L298N1.IN2
  N18: A1.Pin_32, L298N1.ENA
  N19: Yumo-enc1.A, Часть1.C0
  N20: Yumo-enc1.B, Часть1.C1
  N21: Yumo-enc1.Z, Часть1.C2
  N22: L298N1.OUT1, M4.pin_2
  N23: L298N1.OUT2, M4.pin_1
  N24: L298N1.OUT3, M3.pin_1
  N25: L298N1.OUT4, M3.pin_2
  12V: L298N1.12V, L298N2.12V, Power_plug2.VCC
  N26: M1.pin_1, L298N2.OUT3
  N27: M1.pin_2, L298N2.OUT4
  N28: Yumo-enc2.A, Часть1.C5
  N29: Yumo-enc2.B, Часть1.C4
  N30: Yumo-enc2.Z, Часть1.C3
  N31: M2.pin_1, L298N2.OUT2
  N32: M2.pin_2, L298N2.OUT1
  N33: Yumo-enc3.A, Часть1.C8
  N34: Yumo-enc3.B, Часть1.C7
  N35: Yumo-enc3.Z, Часть1.C6
  N36: S1.S, Часть1.C9
  N37: S2.S, Часть1.C10
  N38: S3.S, Часть1.C11
  N39: S4.S, Часть1.C12
  N40: S5.S, Часть1.C13

notes:
  5V DC
  24V DC
  Y-ось
  X-ось
  Z-ось

custom parts:
  Wemos S2 Mini: A mini wifi board based on the ESP32-S2FN4R2.
  YumoE6B2: Yumo E6B2-C incremental encoder. Resolutions 10 to 4000 pulses per revolution (depending on model number). Power from 5 to 24V (again depending on model). Dia 40mm body 30mm plus 20mm shaft.
  L298N DC motor driver: 2x DC motor driver with 78M05 positive voltage regulator (7..35 V) L298N: max 46 V, 2 A Set 5 V Enable jumper to enable 5 V regultor (needed for the L298N) and +5 V output at screw terminal or supply external +5 V at screw terminal Set ENA and/or ENB to +5 V to enable motor permanently or supply ENA and/or ENB with PWM signal IN1 and IN2 set rotation directory for motor A (OUT1/OUT2) IN2 and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
  Limit Switch: Generic limit switch commonly found on 3D printers. Typical lever microswitch mounted on a PCB board with a 3 pin JST XH connector.
