# Fritzing sketch Поворотный конвейер (saved by Fritzing 0.9.3b)

parts:
  Power_plug1 = Power plug
  Power_plug2 = Power plug
  M1 = DC Motor
  L298N1 = L298N DC motor driver
  A1 = Wemos S2 Mini [part_number="WeMos D1 Mini Lite"]
  Часть1 = VL530X Time of Flight Distance Sensor [part_number="tonetoys #3317"]
  M3 = DC Motor
  A2 = AS5600 module

nets:
  GND: Power_plug1.GND, Power_plug2.GND, L298N1.GND, A1.Pin_18, A1.Pin_26, Часть1.GND
  VCC: Power_plug1.VCC, L298N1.5V, A1.Pin_17, Часть1.VCC
  VCC_2: Power_plug2.VCC, L298N1.12V
  N1: M1.pin_1, L298N1.OUT2
  N2: M1.pin_2, L298N1.OUT1
  N3: L298N1.OUT3, M3.pin_1
  N4: L298N1.OUT4, M3.pin_2
  N5: L298N1.ENA, A1.Pin_32
  N6: L298N1.ENB, A1.Pin_15
  N7: L298N1.IN1, A1.Pin_24
  N8: L298N1.IN2, A1.Pin_23
  N9: L298N1.IN3, A1.Pin_6
  N10: L298N1.IN4, A1.Pin_7
  N11: A1.Pin_5, Часть1.SCL
  N12: A1.Pin_13, Часть1.SDA
  N13: A1.Pin_31, A2.Pin_2

notes:
  24V DC
  5V DC

custom parts:
  L298N DC motor driver: 2x DC motor driver with 78M05 positive voltage regulator (7..35 V) L298N: max 46 V, 2 A Set 5 V Enable jumper to enable 5 V regultor (needed for the L298N) and +5 V output at screw terminal or supply external +5 V at screw terminal Set ENA and/or ENB to +5 V to enable motor permanently or supply ENA and/or ENB with PWM signal IN1 and IN2 set rotation directory for motor A (OUT1/OUT2) IN2 and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
  Wemos S2 Mini: A mini wifi board based on the ESP32-S2FN4R2.
  VL530X Time of Flight Distance Sensor: Time of flight sensor
  AS5600 module: .This module is mainly placed behind the stepper motor to obtain the rotation angle of the stepper motor.
